# Fritzing sketch reader (saved by Fritzing 0.9.3b)
breadboards: 1

parts:
  R1 = Photocell (LDR) [package=THT]
  R2 = Photocell (LDR) [package=THT]
  R3 = Photocell (LDR) [package=THT]
  R4 = Photocell (LDR) [package=THT]
  R5 = Photocell (LDR) [package=THT]
  R6 = Resistor [tolerance=±5% resistance=22k package=THT]
  R7 = Resistor [tolerance=±5% resistance=22k package=THT]
  R8 = Resistor [tolerance=±5% resistance=22k package=THT]
  R9 = Resistor [tolerance=±5% resistance=22k package=THT]
  R10 = Resistor [tolerance=±5% resistance=22k package=THT]
  LED1 = LED - 5mm [color="Green (565nm)" package="5 mm [THT]"]
  LED2 = LED - 5mm [color="Green (565nm)" package="5 mm [THT]"]
  LED3 = LED - 5mm [color="Green (565nm)" package="5 mm [THT]"]
  LED4 = LED - 5mm [color="Green (565nm)" package="5 mm [THT]"]
  LED5 = LED - 5mm [color="Green (565nm)" package="5 mm [THT]"]
  U1 = atmega328 [package=dip]

nets:
  N1: R1.pin_0, R2.pin_0, R3.pin_0, R4.pin_0, R5.pin_0, U1.VCC
  N2: R1.pin_1, R10.Pin_0, U1.A1
  N3: R2.pin_1, R9.Pin_0, U1.A0
  N4: R3.pin_1, R8.Pin_0, U1.A3
  N5: R4.pin_1, R7.Pin_0, U1.A4
  N6: R5.pin_1, R6.Pin_0, U1.A2
  N7: R6.Pin_1, R7.Pin_1, R8.Pin_1, R9.Pin_1, R10.Pin_1
  N8: LED1.cathode, LED2.cathode, LED3.cathode, LED4.cathode, LED5.cathode, U1.GND#7
  N9: LED1.anode, LED5.anode
  N10: LED3.anode, U1.D13

notes:
  These LEDs are connected to Digital Pin 13
  These wires go to AnalogIn pins
  ATMega328 is an example of a microprocessor which could be used to control the reader, and is what we used.
